// Logisim project vertebrate.circ as structural Verilog
module CPU (
  input  [15:0] din,
  input  clk,
  input  INT,
  output MEMLD,
  output INTACK,
  output [15:0] Dout,
  output [11:0] Addrout
);

  wire ALUz, INTLD, IRLD, multiplexer_1_out, MUX, or_1_out, PCINC, PCLD, PCMUX, REGLD, SP_minus, SP_plus, Z,
       ZFLD, ZFPOP;
  wire [1:0] ARMUX, DATAMUX;
  wire [2:0] DR, SR1, SR2;
  wire [3:0] ALUC;
  wire [11:0] adder_1_out, instr, ISR, multiplexer_2_out, PC;
  wire [15:0] ALUout, bit_extender_1_out, bit_extender_2_out, multiplexer_3_out, R1, R2, SP;

  ALU alu_1 (.op1(R1), .op2(R2), .s(ALUC), .out(ALUout), .Z(ALUz));
  Instruction_Decoder instruction_decoder_1 (.instr(instr), .dr(DR), .sr1(SR1), .sr2(SR2), .ALUC(ALUC));
  IR ir_1 (.ld(din[11:0]), .en(IRLD), .clk(clk), .rd(instr));
  or or_1 (or_1_out, ZFLD, ZFPOP);
  Multiplexer #(.enable("false")) multiplexer_1 (.in0(din[0]), .in1(ALUz), .out(multiplexer_1_out), .sel(ZFLD));
  ZF zf_1 (.ld(multiplexer_1_out), .en(or_1_out), .clk(clk), .rd(Z));
  Adder #(.width(12)) adder_1 (.a(instr), .b(PC), .out(adder_1_out));  // open: cin, cout
  Multiplexer #(.width(12), .enable("false")) multiplexer_2 (
    .in0(adder_1_out), .in1(din[11:0]), .out(multiplexer_2_out), .sel(PCMUX));
  Multiplexer #(.width(16), .enable("false")) multiplexer_3 (
    .in0(ALUout), .in1(din), .out(multiplexer_3_out), .sel(MUX));
  // PC pc_1: pin names not known; wires that end beside it: multiplexer_2_out, PCLD, clk, PCINC, PC
  Interrupt_Descriptor_Table interrupt_descriptor_table_1 (.INTV(din[2:0]), .INTLD(INTLD), .clk(clk), .ISR(ISR));
  Register_File register_file_1 (
    .ld(multiplexer_3_out), .clk(clk), .sr1(SR1), .sr2(SR2), .R1(R1), .R2(R2), .sw(DR), .en(REGLD), .SP(SP),
    .SP_plus(SP_plus), .SP_minus(SP_minus));
  Control_Unit control_unit_1 (
    .Z(Z), .opc(din[15:12]), .clk(clk), .INT(INT), .INTACK(INTACK), .DATAMUX(DATAMUX), .ARMUX(ARMUX),
    .PCMUX(PCMUX), .MUX(MUX), .PCINC(PCINC), .SP_plus(SP_plus), .SP_minus(SP_minus), .ZFPOP(ZFPOP),
    .ZFLD(ZFLD), .INTLD(INTLD), .MEMLD(MEMLD), .REGLD(REGLD), .PCLD(PCLD), .IRLD(IRLD));
  assign bit_extender_1_out = {{4{1'b0}}, PC};  // Bit_Extender bit_extender_1
  Multiplexer #(.select(2), .width(16), .enable("false")) multiplexer_4 (
    .in0(R2), .in1(bit_extender_1_out), .in2(bit_extender_2_out), .out(Dout), .sel(DATAMUX));  // open: in3
  assign bit_extender_2_out = {{15{1'b0}}, Z};  // Bit_Extender bit_extender_2
  Multiplexer #(.select(2), .width(12), .enable("false")) multiplexer_5 (
    .in0(PC), .in1(R1[11:0]), .in2(SP[11:0]), .in3(ISR), .out(Addrout), .sel(ARMUX));

  // Notes on the sheet:
  //   Input
  //   Output
endmodule

module ALU_1 (
  input  op1,
  input  op2,
  input  cin,
  input  [2:0] s,
  output cout,
  output out
);

  wire and_1_out, and_2_out, and_3_out, not_1_out, or_1_out, xor_1_out, xor_2_out, xor_3_out;

  xor xor_1 (xor_1_out, op1, op2);
  and and_1 (and_1_out, xor_1_out, cin);
  and and_2 (and_2_out, op2, op1);
  and and_3 (and_3_out, op1, op2);
  or or_1 (or_1_out, op1, op2);
  not not_1 (not_1_out, op1);
  xor xor_2 (xor_2_out, xor_1_out, cin);
  xor xor_3 (xor_3_out, op1, op2);
  or or_2 (cout, and_1_out, and_2_out);
  Multiplexer #(.select(3), .enable("false")) multiplexer_1 (
    .in0(xor_2_out), .in1(and_3_out), .in2(or_1_out), .in3(xor_3_out), .in4(not_1_out), .in5(op1), .out(out),
    .sel(s));  // open: in6, in7
endmodule

module ALU (
  input  [15:0] op1,
  input  [15:0] op2,
  input  [3:0] s,
  output [15:0] out,
  output Z
);

  wire alu_1_1_cout, alu_1_2_cout, alu_1_3_cout, alu_1_4_cout, alu_1_5_cout, alu_1_6_cout, alu_1_7_cout,
       alu_1_8_cout, alu_1_9_cout, alu_1_10_cout, alu_1_11_cout, alu_1_12_cout, alu_1_13_cout, alu_1_14_cout,
       alu_1_15_cout, and_1_out, and_2_out, and_3_out, and_4_out, and_5_out, and_6_out, and_7_out, and_8_out,
       and_9_out, and_10_out, not_1_out, not_2_out, not_3_out, not_4_out, not_5_out, not_6_out, not_7_out,
       not_8_out, not_9_out, not_10_out, not_11_out, not_12_out, not_13_out;
  wire [1:0] or_5_out;
  wire [2:0] or_1_out;
  wire [15:0] multiplexer_1_out, not_14_out;

  not not_1 (not_1_out, s[0]);
  not not_2 (not_2_out, s[1]);
  not not_3 (not_3_out, s[0]);
  not not_4 (not_4_out, s[3]);
  not not_5 (not_5_out, s[3]);
  not not_6 (not_6_out, s[1]);
  not not_7 (not_7_out, s[2]);
  not not_8 (not_8_out, s[0]);
  not not_9 (not_9_out, s[2]);
  not not_10 (not_10_out, s[1]);
  not not_11 (not_11_out, s[2]);
  not not_12 (not_12_out, s[3]);
  not not_13 (not_13_out, s[2]);
  and and_1 (and_1_out, ~s[3], ~s[2], ~s[1], s[0]);  // AND_Gate
  and and_2 (and_2_out, not_1_out, not_2_out, s[3]);
  and and_3 (and_3_out, not_3_out, s[1], not_4_out);
  and and_4 (and_4_out, s[0], s[1], not_5_out);
  and and_5 (and_5_out, not_6_out, s[3]);
  and and_6 (and_6_out, s[0], s[2]);
  and and_7 (and_7_out, s[3], s[1], not_7_out, not_8_out);
  and and_8 (and_8_out, s[3], s[1], s[0], not_9_out);
  and and_9 (and_9_out, s[0], not_10_out, not_11_out, not_12_out);
  and and_10 (and_10_out, s[0], s[1], s[3], not_13_out);
  or or_1 (or_1_out[0], and_2_out, s[2], and_3_out);
  or or_2 (or_1_out[1], s[2], and_4_out);
  or or_3 (or_1_out[2], and_5_out, and_6_out);
  or or_4 (or_5_out[1], and_7_out, and_8_out);
  or or_5 (or_5_out[0], and_9_out, and_10_out);
  assign not_14_out = ~op2;  // NOT_Gate not_14, 16 bits wide
  Multiplexer #(.select(2), .width(16), .enable("false")) multiplexer_1 (
    .in0(op2), .in1(not_14_out), .in2(16'h1), .in3({16{1'b1}}), .out(multiplexer_1_out), .sel(or_5_out));
  ALU_1 alu_1_1 (
    .op1(op1[0]), .op2(multiplexer_1_out[0]), .cin(and_1_out), .cout(alu_1_1_cout), .out(out[0]), .s(or_1_out));
  ALU_1 alu_1_2 (
    .op1(op1[1]), .op2(multiplexer_1_out[1]), .cin(alu_1_1_cout), .cout(alu_1_2_cout), .out(out[1]),
    .s(or_1_out));
  ALU_1 alu_1_3 (
    .op1(op1[2]), .op2(multiplexer_1_out[2]), .cin(alu_1_2_cout), .cout(alu_1_3_cout), .out(out[2]),
    .s(or_1_out));
  ALU_1 alu_1_4 (
    .op1(op1[3]), .op2(multiplexer_1_out[3]), .cin(alu_1_3_cout), .cout(alu_1_4_cout), .out(out[3]),
    .s(or_1_out));
  ALU_1 alu_1_5 (
    .op1(op1[4]), .op2(multiplexer_1_out[4]), .cin(alu_1_4_cout), .cout(alu_1_5_cout), .out(out[4]),
    .s(or_1_out));
  ALU_1 alu_1_6 (
    .op1(op1[5]), .op2(multiplexer_1_out[5]), .cin(alu_1_5_cout), .cout(alu_1_6_cout), .out(out[5]),
    .s(or_1_out));
  ALU_1 alu_1_7 (
    .op1(op1[6]), .op2(multiplexer_1_out[6]), .cin(alu_1_6_cout), .cout(alu_1_7_cout), .out(out[6]),
    .s(or_1_out));
  ALU_1 alu_1_8 (
    .op1(op1[7]), .op2(multiplexer_1_out[7]), .cin(alu_1_7_cout), .cout(alu_1_8_cout), .out(out[7]),
    .s(or_1_out));
  ALU_1 alu_1_9 (
    .op1(op1[8]), .op2(multiplexer_1_out[8]), .cin(alu_1_8_cout), .cout(alu_1_9_cout), .out(out[8]),
    .s(or_1_out));
  ALU_1 alu_1_10 (
    .op1(op1[9]), .op2(multiplexer_1_out[9]), .cin(alu_1_9_cout), .cout(alu_1_10_cout), .out(out[9]),
    .s(or_1_out));
  ALU_1 alu_1_11 (
    .op1(op1[10]), .op2(multiplexer_1_out[10]), .cin(alu_1_10_cout), .cout(alu_1_11_cout), .out(out[10]),
    .s(or_1_out));
  ALU_1 alu_1_12 (
    .op1(op1[11]), .op2(multiplexer_1_out[11]), .cin(alu_1_11_cout), .cout(alu_1_12_cout), .out(out[11]),
    .s(or_1_out));
  ALU_1 alu_1_13 (
    .op1(op1[12]), .op2(multiplexer_1_out[12]), .cin(alu_1_12_cout), .cout(alu_1_13_cout), .out(out[12]),
    .s(or_1_out));
  ALU_1 alu_1_14 (
    .op1(op1[13]), .op2(multiplexer_1_out[13]), .cin(alu_1_13_cout), .cout(alu_1_14_cout), .out(out[13]),
    .s(or_1_out));
  ALU_1 alu_1_15 (
    .op1(op1[14]), .op2(multiplexer_1_out[14]), .cin(alu_1_14_cout), .cout(alu_1_15_cout), .out(out[14]),
    .s(or_1_out));
  ALU_1 alu_1_16 (
    .op1(op1[15]), .op2(multiplexer_1_out[15]), .cin(alu_1_15_cout), .out(out[15]), .s(or_1_out));  // open: cout
  Comparator #(.width(16), .mode("unsigned")) comparator_1 (.a(out), .b({16{1'b0}}), .eq(Z));  // open: gt, lt
endmodule

module PC (
  input  [11:0] ld,
  input  PCLD,
  input  PCINC,
  input  clk,
  output [11:0] rd
);

  wire or_1_out;
  wire [11:0] adder_1_out, multiplexer_1_out;

  Multiplexer #(.width(12), .enable("false")) multiplexer_1 (
    .in0(adder_1_out), .in1(ld), .out(multiplexer_1_out), .sel(PCLD));
  Register_12 register_12_1 (.ld(multiplexer_1_out), .en(or_1_out), .clk(clk), .rd(rd));
  or or_1 (or_1_out, PCLD, PCINC);
  Adder #(.width(12)) adder_1 (.a(12'h1), .b(rd), .out(adder_1_out));  // open: cin, cout
endmodule

module Register_File (
  input  en,
  input  [2:0] sw,
  input  [15:0] ld,
  input  SP_plus,
  input  SP_minus,
  input  clk,
  input  [2:0] sr1,
  input  [2:0] sr2,
  output [15:0] R1,
  output [15:0] SP,
  output [15:0] R2
);

  wire demultiplexer_1_out0, demultiplexer_1_out1, demultiplexer_1_out2, demultiplexer_1_out3,
       demultiplexer_1_out4, demultiplexer_1_out5, demultiplexer_1_out6, demultiplexer_1_out7, or_1_out,
       or_2_out;
  wire [15:0] adder_1_out, multiplexer_1_out, multiplexer_2_out, register_16_2_rd, register_16_3_rd,
       register_16_4_rd, register_16_5_rd, register_16_6_rd, register_16_7_rd, register_16_8_rd;

  Multiplexer #(.width(16), .enable("false")) multiplexer_1 (
    .in0({16{1'b1}}), .in1(16'h1), .out(multiplexer_1_out), .sel(SP_plus));
  Adder #(.width(16)) adder_1 (.a(multiplexer_1_out), .b(SP), .out(adder_1_out));  // open: cin, cout
  or or_1 (or_1_out, SP_plus, SP_minus);
  Multiplexer #(.width(16), .enable("false")) multiplexer_2 (
    .in0(ld), .in1(adder_1_out), .out(multiplexer_2_out), .sel(or_1_out));
  or or_2 (or_2_out, demultiplexer_1_out7, or_1_out);
  Register_16 register_16_1 (.ld(multiplexer_2_out), .en(or_2_out), .clk(clk), .rd(SP));
  Register_16 register_16_2 (.ld(ld), .en(demultiplexer_1_out6), .clk(clk), .rd(register_16_2_rd));
  Multiplexer #(.select(3), .width(16), .enable("false")) multiplexer_3 (
    .in0(register_16_8_rd), .in1(register_16_7_rd), .in2(register_16_6_rd), .in3(register_16_5_rd),
    .in4(register_16_4_rd), .in5(register_16_3_rd), .in6(register_16_2_rd), .in7(SP), .out(R1), .sel(sr1));
  Register_16 register_16_3 (.ld(ld), .en(demultiplexer_1_out5), .clk(clk), .rd(register_16_3_rd));
  Register_16 register_16_4 (.ld(ld), .en(demultiplexer_1_out4), .clk(clk), .rd(register_16_4_rd));
  Demultiplexer #(.select(3), .enable("false")) demultiplexer_1 (
    .out0(demultiplexer_1_out0), .out1(demultiplexer_1_out1), .out2(demultiplexer_1_out2),
    .out3(demultiplexer_1_out3), .out4(demultiplexer_1_out4), .out5(demultiplexer_1_out5),
    .out6(demultiplexer_1_out6), .out7(demultiplexer_1_out7), .in(en), .sel(sw));
  Register_16 register_16_5 (.ld(ld), .en(demultiplexer_1_out3), .clk(clk), .rd(register_16_5_rd));
  Register_16 register_16_6 (.ld(ld), .en(demultiplexer_1_out2), .clk(clk), .rd(register_16_6_rd));
  Register_16 register_16_7 (.ld(ld), .en(demultiplexer_1_out1), .clk(clk), .rd(register_16_7_rd));
  Register_16 register_16_8 (.ld(ld), .en(demultiplexer_1_out0), .clk(clk), .rd(register_16_8_rd));
  Multiplexer #(.select(3), .width(16), .enable("false")) multiplexer_4 (
    .in0(register_16_8_rd), .in1(register_16_7_rd), .in2(register_16_6_rd), .in3(register_16_5_rd),
    .in4(register_16_4_rd), .in5(register_16_3_rd), .in6(register_16_2_rd), .in7(SP), .out(R2), .sel(sr2));
endmodule

module Register_12 (
  input  [11:0] ld,
  input  en,
  input  clk,
  output [11:0] rd
);

  D_Flip_Flop d_ff_1 (.D(ld[10]), .clk(clk), .Q(rd[10]), .en(en));  // open: clr
  D_Flip_Flop d_ff_2 (.D(ld[11]), .clk(clk), .Q(rd[11]), .en(en));  // open: clr
  D_Flip_Flop d_ff_3 (.D(ld[9]), .clk(clk), .Q(rd[9]), .en(en));  // open: clr
  D_Flip_Flop d_ff_4 (.D(ld[8]), .clk(clk), .Q(rd[8]), .en(en));  // open: clr
  D_Flip_Flop d_ff_5 (.D(ld[7]), .clk(clk), .Q(rd[7]), .en(en));  // open: clr
  D_Flip_Flop d_ff_6 (.D(ld[6]), .clk(clk), .Q(rd[6]), .en(en));  // open: clr
  D_Flip_Flop d_ff_7 (.D(ld[5]), .clk(clk), .Q(rd[5]), .en(en));  // open: clr
  D_Flip_Flop d_ff_8 (.D(ld[4]), .clk(clk), .Q(rd[4]), .en(en));  // open: clr
  D_Flip_Flop d_ff_9 (.D(ld[3]), .clk(clk), .Q(rd[3]), .en(en));  // open: clr
  D_Flip_Flop d_ff_10 (.D(ld[1]), .clk(clk), .Q(rd[1]), .en(en));  // open: clr
  D_Flip_Flop d_ff_11 (.D(ld[2]), .clk(clk), .Q(rd[2]), .en(en));  // open: clr
  D_Flip_Flop d_ff_12 (.D(ld[0]), .clk(clk), .Q(rd[0]), .en(en));  // open: clr
endmodule

module Register_16 (
  input  [15:0] ld,
  input  en,
  input  clk,
  output [15:0] rd
);

  D_Flip_Flop d_ff_1 (.D(ld[14]), .clk(clk), .Q(rd[14]), .en(en));  // open: clr
  D_Flip_Flop d_ff_2 (.D(ld[15]), .clk(clk), .Q(rd[15]), .en(en));  // open: clr
  D_Flip_Flop d_ff_3 (.D(ld[13]), .clk(clk), .Q(rd[13]), .en(en));  // open: clr
  D_Flip_Flop d_ff_4 (.D(ld[12]), .clk(clk), .Q(rd[12]), .en(en));  // open: clr
  D_Flip_Flop d_ff_5 (.D(ld[10]), .clk(clk), .Q(rd[10]), .en(en));  // open: clr
  D_Flip_Flop d_ff_6 (.D(ld[11]), .clk(clk), .Q(rd[11]), .en(en));  // open: clr
  D_Flip_Flop d_ff_7 (.D(ld[9]), .clk(clk), .Q(rd[9]), .en(en));  // open: clr
  D_Flip_Flop d_ff_8 (.D(ld[8]), .clk(clk), .Q(rd[8]), .en(en));  // open: clr
  D_Flip_Flop d_ff_9 (.D(ld[7]), .clk(clk), .Q(rd[7]), .en(en));  // open: clr
  D_Flip_Flop d_ff_10 (.D(ld[5]), .clk(clk), .Q(rd[5]), .en(en));  // open: clr
  D_Flip_Flop d_ff_11 (.D(ld[6]), .clk(clk), .Q(rd[6]), .en(en));  // open: clr
  D_Flip_Flop d_ff_12 (.D(ld[4]), .clk(clk), .Q(rd[4]), .en(en));  // open: clr
  D_Flip_Flop d_ff_13 (.D(ld[3]), .clk(clk), .Q(rd[3]), .en(en));  // open: clr
  D_Flip_Flop d_ff_14 (.D(ld[1]), .clk(clk), .Q(rd[1]), .en(en));  // open: clr
  D_Flip_Flop d_ff_15 (.D(ld[2]), .clk(clk), .Q(rd[2]), .en(en));  // open: clr
  D_Flip_Flop d_ff_16 (.D(ld[0]), .clk(clk), .Q(rd[0]), .en(en));  // open: clr
endmodule

module D_Flip_Flop (
  input  D,
  input  clk,
  input  en,
  input  clr,
  output Q
);

  wire not_1_out;

  not not_1 (not_1_out, D);
  S_R_Flip_Flop s_r_ff_1 (.S(D), .clk(clk), .R(not_1_out), .Q(Q), .reset(clr), .en(en));  // open: Qn, preset
endmodule

module Instruction_Decoder (
  input  [11:0] instr,
  output [2:0] dr,
  output [2:0] sr1,
  output [2:0] sr2,
  output [3:0] ALUC
);

  wire and_1_out;
  wire [3:0] bit_extender_1_out;

  and and_1 (and_1_out, instr[10], instr[11]);
  assign bit_extender_1_out = {{1{1'b0}}, instr[11:9]};  // Bit_Extender bit_extender_1
  Multiplexer #(.width(4), .enable("false")) multiplexer_1 (
    .in0(bit_extender_1_out), .in1(instr[9:6]), .out(ALUC), .sel(and_1_out));

  assign dr = instr[2:0];
  assign sr1 = instr[5:3];
  assign sr2 = instr[8:6];
endmodule

module IR (
  input  [11:0] ld,
  input  en,
  input  clk,
  output [11:0] rd
);

  Register_12 register_12_1 (.ld(ld), .en(en), .clk(clk), .rd(rd));
endmodule

module ZF (
  input  ld,
  input  en,
  input  clk,
  output rd
);

  D_Flip_Flop d_ff_1 (.D(ld), .clk(clk), .Q(rd), .en(en));  // open: clr
endmodule

module _7_Segment_Hex_Adapter (
  input  [3:0] num,
  output [2:0] edc,
  output [3:0] gfab
);

  wire and_1_out, and_2_out, and_3_out, and_4_out, and_5_out, and_6_out, and_7_out, and_8_out, and_9_out,
       and_10_out, and_11_out, and_12_out, and_13_out, and_14_out, and_15_out, and_16_out, and_17_out,
       and_18_out, and_19_out, and_20_out, and_21_out, and_22_out, and_23_out, and_24_out, and_25_out,
       and_26_out, and_27_out, and_28_out, and_29_out, and_30_out, and_31_out, and_32_out, and_33_out,
       and_34_out, and_35_out, not_1_out, not_2_out, not_3_out, not_4_out, not_5_out, not_6_out, not_7_out,
       not_8_out, not_9_out, not_10_out, not_11_out, not_12_out, not_13_out, not_14_out, not_15_out,
       not_16_out, not_17_out, not_18_out, not_19_out, not_20_out, not_21_out, not_22_out, not_23_out,
       not_24_out, not_25_out, not_26_out, not_27_out, not_28_out, not_29_out, not_30_out, not_31_out,
       not_32_out, not_33_out, not_34_out, not_35_out, not_36_out, not_37_out, not_38_out, not_39_out,
       not_40_out, not_41_out, not_42_out, not_43_out;

  not not_1 (not_1_out, num[2]);
  and and_1 (and_1_out, not_1_out, not_2_out);
  not not_2 (not_2_out, num[0]);
  not not_3 (not_3_out, num[3]);
  and and_2 (and_2_out, not_3_out, num[1]);
  not not_4 (not_4_out, num[3]);
  and and_3 (and_3_out, not_4_out, num[2], num[0]);
  and and_4 (and_4_out, num[2], num[1]);
  and and_5 (and_5_out, num[3], not_5_out, not_6_out);
  not not_5 (not_5_out, num[2]);
  not not_6 (not_6_out, num[1]);
  and and_6 (and_6_out, num[3], not_7_out);
  not not_7 (not_7_out, num[0]);
  not not_8 (not_8_out, num[3]);
  and and_7 (and_7_out, not_8_out, not_9_out);
  not not_9 (not_9_out, num[2]);
  not not_10 (not_10_out, num[3]);
  not not_11 (not_11_out, num[1]);
  and and_8 (and_8_out, not_10_out, not_11_out, not_12_out);
  not not_12 (not_12_out, num[0]);
  not not_13 (not_13_out, num[2]);
  and and_9 (and_9_out, not_13_out, not_14_out);
  not not_14 (not_14_out, num[0]);
  not not_15 (not_15_out, num[3]);
  and and_10 (and_10_out, not_15_out, num[1], num[0]);
  and and_11 (and_11_out, num[3], not_16_out, num[0]);
  not not_16 (not_16_out, num[1]);
  not not_17 (not_17_out, num[3]);
  and and_12 (and_12_out, not_17_out, not_18_out);
  not not_18 (not_18_out, num[1]);
  not not_19 (not_19_out, num[3]);
  and and_13 (and_13_out, not_19_out, num[0]);
  not not_20 (not_20_out, num[1]);
  and and_14 (and_14_out, not_20_out, num[0]);
  not not_21 (not_21_out, num[3]);
  and and_15 (and_15_out, not_21_out, num[2]);
  and and_16 (and_16_out, num[3], not_22_out);
  not not_22 (not_22_out, num[2]);
  not not_23 (not_23_out, num[3]);
  and and_17 (and_17_out, not_23_out, not_24_out, not_25_out);
  not not_24 (not_24_out, num[2]);
  not not_25 (not_25_out, num[0]);
  not not_26 (not_26_out, num[2]);
  and and_18 (and_18_out, not_26_out, num[1], num[0]);
  not not_27 (not_27_out, num[1]);
  and and_19 (and_19_out, num[2], not_27_out, num[0]);
  and and_20 (and_20_out, num[2], num[1], not_28_out);
  not not_28 (not_28_out, num[0]);
  and and_21 (and_21_out, num[3], not_29_out);
  not not_29 (not_29_out, num[1]);
  not not_30 (not_30_out, num[2]);
  and and_22 (and_22_out, not_30_out, not_31_out);
  not not_31 (not_31_out, num[0]);
  and and_23 (and_23_out, num[1], not_32_out);
  not not_32 (not_32_out, num[0]);
  and and_24 (and_24_out, num[3], num[1]);
  and and_25 (and_25_out, num[3], num[2]);
  not not_33 (not_33_out, num[1]);
  and and_26 (and_26_out, not_33_out, not_34_out);
  not not_34 (not_34_out, num[0]);
  not not_35 (not_35_out, num[3]);
  and and_27 (and_27_out, not_35_out, num[2], not_36_out);
  not not_36 (not_36_out, num[1]);
  and and_28 (and_28_out, num[2], not_37_out);
  not not_37 (not_37_out, num[0]);
  and and_29 (and_29_out, num[3], not_38_out);
  not not_38 (not_38_out, num[2]);
  and and_30 (and_30_out, num[3], num[1]);
  not not_39 (not_39_out, num[2]);
  and and_31 (and_31_out, not_39_out, num[1]);
  and and_32 (and_32_out, num[1], not_40_out);
  not not_40 (not_40_out, num[0]);
  not not_41 (not_41_out, num[3]);
  and and_33 (and_33_out, not_41_out, num[2], not_42_out);
  not not_42 (not_42_out, num[1]);
  and and_34 (and_34_out, num[3], not_43_out);
  not not_43 (not_43_out, num[2]);
  and and_35 (and_35_out, num[3], num[0]);
  or or_1 (gfab[0], and_7_out, and_8_out, and_9_out, and_10_out, and_11_out);
  or or_2 (edc[0], and_12_out, and_13_out, and_14_out, and_15_out, and_16_out);
  or or_3 (edc[1], and_17_out, and_18_out, and_19_out, and_20_out, and_21_out);
  or or_4 (edc[2], and_22_out, and_23_out, and_24_out, and_25_out);
  or or_5 (gfab[2], and_26_out, and_27_out, and_28_out, and_29_out, and_30_out);
  or or_6 (gfab[3], and_31_out, and_32_out, and_33_out, and_34_out, and_35_out);
  or or_7 (gfab[1], and_1_out, and_2_out, and_3_out, and_4_out, and_5_out, and_6_out);
endmodule

module Control_Unit (
  input  Z,
  input  INT,
  input  [3:0] opc,
  input  clk,
  output INTACK,
  output [1:0] DATAMUX,
  output [1:0] ARMUX,
  output PCMUX,
  output MUX,
  output PCINC,
  output SP_plus,
  output SP_minus,
  output ZFPOP,
  output ZFLD,
  output INTLD,
  output MEMLD,
  output REGLD,
  output PCLD,
  output IRLD
);

  wire and_1_out, and_2_out, and_3_out, and_4_out, s_r_ff_1_q;
  wire [1:0] or_1_out;
  wire [4:0] bit_extender_1_out, multiplexer_1_out, register_5_1_rd;
  wire [23:16] rom_1_data;

  assign bit_extender_1_out = {{1{1'b0}}, opc};  // Bit_Extender bit_extender_1
  Multiplexer #(.select(2), .width(5), .enable("false")) multiplexer_1 (
    .in0({5{1'b0}}), .in1(bit_extender_1_out), .in2(rom_1_data[23:19]), .in3(5'b10011),
    .out(multiplexer_1_out), .sel(or_1_out));
  Register_5 register_5_1 (.ld(multiplexer_1_out), .en(1'b1), .clk(clk), .rd(register_5_1_rd));
  ROM #(.addrWidth(5), .dataWidth(24)) rom_1 (
    .addr(register_5_1_rd),
    .data({rom_1_data[23:19], INTACK, rom_1_data[17:16], DATAMUX, ARMUX, PCMUX, MUX, PCINC, SP_plus, SP_minus, ZFPOP, ZFLD, INTLD, MEMLD, REGLD, PCLD, IRLD}),
    .sel(1'b1));
  and and_1 (and_1_out, ~rom_1_data[19], ~rom_1_data[20], ~rom_1_data[21], ~rom_1_data[22], ~rom_1_data[23]);  // AND_Gate
  S_R_Flip_Flop s_r_ff_1 (
    .S(rom_1_data[17]), .R(rom_1_data[16]), .Q(s_r_ff_1_q), .en(1'b1));  // open: clk, Qn, preset, reset
  and and_2 (and_2_out, INT, and_1_out, s_r_ff_1_q);
  and and_3 (and_3_out, ~IRLD, INT, s_r_ff_1_q, and_1_out);  // AND_Gate
  or or_1 (or_1_out[0], and_3_out, and_4_out);
  and and_4 (and_4_out, IRLD, opc[2], ~opc[0], ~Z);  // AND_Gate
  or or_2 (or_1_out[1], ~IRLD, and_2_out);  // OR_Gate

  // Notes on the sheet:
  //   contents of rom_1 (hex, n*v repeats v):
  //   201 604 1404 1008 2 2 0 24 2088 880100 610a 900100 20000 10000 780100 802140 2802 2404 2c02 a16088
  //   aca098 3802
endmodule

module Register_5 (
  input  [4:0] ld,
  input  en,
  input  clk,
  output [4:0] rd
);

  D_Flip_Flop d_ff_1 (.D(ld[4]), .clk(clk), .Q(rd[4]), .en(en));  // open: clr
  D_Flip_Flop d_ff_2 (.D(ld[2]), .clk(clk), .Q(rd[2]), .en(en));  // open: clr
  D_Flip_Flop d_ff_3 (.D(ld[3]), .clk(clk), .Q(rd[3]), .en(en));  // open: clr
  D_Flip_Flop d_ff_4 (.D(ld[1]), .clk(clk), .Q(rd[1]), .en(en));  // open: clr
  D_Flip_Flop d_ff_5 (.D(ld[0]), .clk(clk), .Q(rd[0]), .en(en));  // open: clr
endmodule

module Interrupt_Controller (
  input  IR0,
  input  IR1,
  input  IR2,
  input  IR3,
  input  IR4,
  input  IR5,
  input  IR6,
  input  IR7,
  input  INTACK,
  output [2:0] INTV,
  output INT
);

  wire d_ff_1_q, d_ff_2_q, d_ff_3_q, d_ff_4_q, d_ff_5_q, d_ff_6_q, d_ff_7_q, d_ff_8_q, demultiplexer_1_out0,
       demultiplexer_1_out1, demultiplexer_1_out2, demultiplexer_1_out3, demultiplexer_1_out4,
       demultiplexer_1_out5, demultiplexer_1_out6, demultiplexer_1_out7;
  wire [2:0] priority_encoder_1_out;

  D_Flip_Flop d_ff_1 (.D(1'b1), .clk(IR0), .Q(d_ff_1_q), .en(1'b1), .clr(demultiplexer_1_out0));
  D_Flip_Flop d_ff_2 (.D(1'b1), .clk(IR1), .Q(d_ff_2_q), .en(1'b1), .clr(demultiplexer_1_out1));
  D_Flip_Flop d_ff_3 (.D(1'b1), .clk(IR2), .Q(d_ff_3_q), .en(1'b1), .clr(demultiplexer_1_out2));
  D_Flip_Flop d_ff_4 (.D(1'b1), .clk(IR3), .Q(d_ff_4_q), .en(1'b1), .clr(demultiplexer_1_out3));
  D_Flip_Flop d_ff_5 (.D(1'b1), .clk(IR4), .Q(d_ff_5_q), .en(1'b1), .clr(demultiplexer_1_out4));
  D_Flip_Flop d_ff_6 (.D(1'b1), .clk(IR5), .Q(d_ff_6_q), .en(1'b1), .clr(demultiplexer_1_out5));
  D_Flip_Flop d_ff_7 (.D(1'b1), .clk(IR6), .Q(d_ff_7_q), .en(1'b1), .clr(demultiplexer_1_out6));
  D_Flip_Flop d_ff_8 (.D(1'b1), .clk(IR7), .Q(d_ff_8_q), .en(1'b1), .clr(demultiplexer_1_out7));
  Demultiplexer #(.select(3), .enable("false")) demultiplexer_1 (
    .out0(demultiplexer_1_out0), .out1(demultiplexer_1_out1), .out2(demultiplexer_1_out2),
    .out3(demultiplexer_1_out3), .out4(demultiplexer_1_out4), .out5(demultiplexer_1_out5),
    .out6(demultiplexer_1_out6), .out7(demultiplexer_1_out7), .in(INTACK), .sel(INTV));
  Priority_Encoder priority_encoder_1 (
    .in0(d_ff_1_q), .in1(d_ff_2_q), .in2(d_ff_3_q), .in3(d_ff_4_q), .in4(d_ff_5_q), .in5(d_ff_6_q),
    .in6(d_ff_7_q), .in7(d_ff_8_q), .out(priority_encoder_1_out), .en_in(1'b1), .gs(INT));  // open: en_out
  Register_3 register_3_1 (.ld(priority_encoder_1_out), .en(1'b1), .clk(INTACK), .rd(INTV));
endmodule

module Register_3 (
  input  [2:0] ld,
  input  en,
  input  clk,
  output [2:0] rd
);

  D_Flip_Flop d_ff_1 (.D(ld[2]), .clk(clk), .Q(rd[2]), .en(en));  // open: clr
  D_Flip_Flop d_ff_2 (.D(ld[1]), .clk(clk), .Q(rd[1]), .en(en));  // open: clr
  D_Flip_Flop d_ff_3 (.D(ld[0]), .clk(clk), .Q(rd[0]), .en(en));  // open: clr
endmodule

module Interrupt_Descriptor_Table (
  input  [2:0] INTV,
  input  INTLD,
  input  clk,
  output [11:0] ISR
);

  wire [11:0] adder_1_out, bit_extender_1_out;

  assign bit_extender_1_out = {{9{1'b0}}, INTV};  // Bit_Extender bit_extender_1
  Register_12 register_12_1 (.ld(adder_1_out), .en(INTLD), .clk(clk), .rd(ISR));
  Adder #(.width(12)) adder_1 (.a(12'h7f0), .b(bit_extender_1_out), .out(adder_1_out));  // open: cin, cout
endmodule
